// Logisim project fizz.circ as structural Verilog: 5 circuits, main circuit main
module main (
);

  wire and_1_out, mips_alu_1_p4, registers_1_p2, registers_1_p3, registers_1_p4, undriven_4, undriven_5,
       undriven_6, undriven_7, undriven_8, undriven_10, xor_1_out;
  wire [1:0] undriven_2;
  wire [3:0] instruction_decode_1_opcode, instruction_decode_1_shiftamount, rom_2_data;
  wire [7:0] adder_1_out, adder_2_out, bit_extender_1_out, bit_extender_4_out, multiplexer_1_out,
       multiplexer_2_out, multiplexer_4_out, ram_1_data, register_1_q, registers_1_p1, registers_1_p5,
       registers_1_p6, undriven, undriven_3, undriven_9;
  wire [19:0] rom_1_data;
  wire [31:0] bit_extender_2_out, bit_extender_3_out, mips_alu_1_p5;

  Register register_1 (.D(multiplexer_4_out), .Q(register_1_q));  // open: en, clk, clr
  Adder adder_1 (.a(8'h1), .b(register_1_q), .out(adder_1_out));  // open: cin, cout
  ROM #(.dataWidth(20)) rom_1 (.addr(register_1_q), .data(rom_1_data));  // open: sel
  Instruction_Decode instruction_decode_1 (
    .in_1(rom_1_data), .shiftAmount(instruction_decode_1_shiftamount), .opCode(instruction_decode_1_opcode));  // open: DstReg, Address_Imm, SrcReg2, SrcReg1, TargetJump
  // Registers registers_1: pin names not known; wires that end beside it: registers_1_p1, registers_1_p2, registers_1_p3, registers_1_p4, registers_1_p5, registers_1_p6
  assign bit_extender_1_out = {{4{instruction_decode_1_shiftamount[3]}}, instruction_decode_1_shiftamount};  // Bit_Extender bit_extender_1
  assign bit_extender_2_out = {{24{registers_1_p5[7]}}, registers_1_p5};  // Bit_Extender bit_extender_2
  Multiplexer #(.select(2), .width(8), .enable("false")) multiplexer_1 (
    .in0(registers_1_p6), .in1(undriven), .in2(bit_extender_1_out), .in3(bit_extender_1_out),
    .out(multiplexer_1_out), .sel(undriven_2));
  ROM #(.addrWidth(4), .dataWidth(4)) rom_2 (.addr(instruction_decode_1_opcode), .data(rom_2_data));  // open: sel
  assign bit_extender_3_out = {{24{multiplexer_1_out[7]}}, multiplexer_1_out};  // Bit_Extender bit_extender_3
  // MIPS_ALU mips_alu_1: pin names not known; wires that end beside it: bit_extender_2_out, bit_extender_3_out, rom_2_data, mips_alu_1_p4, mips_alu_1_p5
  Bit_Extender #(.in_width(32), .out_width(8), .\type ("sign")) bit_extender_4 (
    .in(mips_alu_1_p5), .out(bit_extender_4_out));
  Adder adder_2 (.a(adder_1_out), .b(undriven_3), .out(adder_2_out));  // open: cin, cout
  xor xor_1 (xor_1_out, mips_alu_1_p4, undriven_4);
  RAM #(.bus("separate")) ram_1 (
    .addr(bit_extender_4_out), .din(registers_1_p6), .data(ram_1_data), .str(undriven_5), .ld(undriven_6));  // open: sel, clk, clr
  Multiplexer #(.width(8), .enable("false")) multiplexer_2 (
    .in0(adder_1_out), .in1(adder_2_out), .out(multiplexer_2_out), .sel(and_1_out));
  and and_1 (and_1_out, xor_1_out, undriven_7);
  Multiplexer #(.width(8)) multiplexer_3 (
    .in0(bit_extender_4_out), .in1(ram_1_data), .out(registers_1_p1), .sel(undriven_8));  // open: en
  Multiplexer #(.width(8), .enable("false")) multiplexer_4 (
    .in0(multiplexer_2_out), .in1(undriven_9), .out(multiplexer_4_out), .sel(undriven_10));

  // Notes on the sheet:
  //   PC
  //   opcode
  //   contents of rom_2 (hex, n*v repeats v):
  //   f 6 6 2 6 2 2 2 1 8 9 6 c 0 1
  //   immediate value/address
  //   shamt
  //   if shift
  //   MAKE ALU 8 BIT AGAIN
  //   ALU SRC
  //   branching
  //   branch address
  //   MEM WRITE
  //   bneq
  //   MEM READ
  //   bneq OR beq
  //   JUMP ADDRESS
  //   MEM TO REG
  //   JUMP
endmodule

module Abro_Logical_Unit (
  input  [7:0] in_1,
  input  [7:0] in_2,
  input  [2:0] in_3,
  output [7:0] out_4
);

  wire [7:0] adder_1_out, and_1_out, nor_1_out, or_1_out, subtractor_1_out;

  Adder adder_1 (.a(in_1), .b(in_2), .out(adder_1_out));  // open: cin, cout
  Subtractor subtractor_1 (.a(in_1), .b(in_2), .out(subtractor_1_out));  // open: bin, bout
  assign and_1_out = in_1 & in_2;  // AND_Gate and_1, 8 bits wide
  assign or_1_out = in_1 | in_2;  // OR_Gate or_1, 8 bits wide
  assign nor_1_out = ~(in_1 | in_2);  // NOR_Gate nor_1, 8 bits wide
  Multiplexer #(.select(3), .width(8)) multiplexer_1 (
    .in0(adder_1_out), .in1(subtractor_1_out), .in2(and_1_out), .in3(or_1_out), .in4(nor_1_out), .out(out_4),
    .sel(in_3));  // open: in5, in6, in7, en
endmodule

module Registers (
  input  clock,
  input  [7:0] data_in,
  input  regWrite,
  input  [3:0] addressA,
  input  [3:0] addressB__ReadOnly,
  output [7:0] data_out_A,
  output [7:0] data_out_B
);

  wire demultiplexer_1_out0, demultiplexer_1_out1, demultiplexer_1_out2, demultiplexer_1_out3,
       demultiplexer_1_out4, demultiplexer_1_out10, demultiplexer_1_out14;
  wire [7:0] SP_q, t0_q, t1_q, t2_q, t3_q, t4_q, ZERO_q;

  Demultiplexer #(.select(4)) demultiplexer_1 (
    .out0(demultiplexer_1_out0), .out1(demultiplexer_1_out1), .out2(demultiplexer_1_out2),
    .out3(demultiplexer_1_out3), .out4(demultiplexer_1_out4), .out10(demultiplexer_1_out10),
    .out14(demultiplexer_1_out14), .out15(demultiplexer_1_out14), .in(regWrite), .sel(addressA));  // open: out5, out6, out7, out8, out9, out11, out12, out13, en
  Register #(.trigger("falling")) t0 (.D(data_in), .en(demultiplexer_1_out0), .Q(t0_q), .clk(clock));  // open: clr
  Register #(.trigger("falling")) t1 (.D(data_in), .en(demultiplexer_1_out1), .Q(t1_q), .clk(clock));  // open: clr
  Register #(.trigger("falling")) t2 (.D(data_in), .en(demultiplexer_1_out3), .Q(t2_q), .clk(clock));  // open: clr
  Register #(.trigger("falling")) t3 (.D(data_in), .en(demultiplexer_1_out2), .Q(t3_q), .clk(clock));  // open: clr
  Register #(.trigger("falling")) t4 (.D(data_in), .en(demultiplexer_1_out4), .Q(t4_q), .clk(clock));  // open: clr
  Register #(.trigger("falling")) ZERO (
    .D({8{1'b0}}), .en(demultiplexer_1_out14), .Q(ZERO_q), .clk(clock));  // open: clr
  Register #(.trigger("falling")) SP (.D(data_in), .en(demultiplexer_1_out10), .Q(SP_q), .clk(clock));  // open: clr
  Multiplexer #(.select(4), .width(8), .enable("false")) multiplexer_1 (
    .in0(t0_q), .in1(t1_q), .in2(t2_q), .in3(t3_q), .in4(t4_q), .in15(ZERO_q), .out(data_out_A),
    .sel(addressA));  // open: in5, in6, in7, in8, in9, in10, in11, in12, in13, in14
  Multiplexer #(.select(4), .width(8)) multiplexer_2 (
    .in0(t0_q), .in1(t1_q), .in2(t2_q), .in3(t3_q), .in4(t4_q), .in10(SP_q), .in15(ZERO_q), .out(data_out_B),
    .sel(addressB__ReadOnly));  // open: in5, in6, in7, in8, in9, in11, in12, in13, in14, en
endmodule

module Control (
  input  [3:0] in_1,
  output Shift,
  output RegDest,
  output Jump,
  output Branch,
  output MemRead,
  output MemToReg,
  output MemWrite,
  output ALUSrc,
  output RegWrite
);

  ROM #(.addrWidth(4), .dataWidth(9)) rom_1 (
    .addr(in_1), .data({RegWrite, ALUSrc, MemWrite, MemToReg, MemRead, Branch, Jump, RegDest, Shift}));  // open: sel

  // Notes on the sheet:
  //   contents of rom_1 (hex, n*v repeats v):
  //   40 20 3 3 81 81 1b 6 3 181 181 20 81 81 81 3
endmodule

module Instruction_Decode (
  input  [19:0] in_1,
  output [3:0] shiftAmount,
  output [3:0] DstReg,
  output [7:0] Address_Imm,
  output [3:0] SrcReg2,
  output [3:0] SrcReg1,
  output [7:0] TargetJump,
  output [3:0] opCode
);


  assign Address_Imm = in_1[7:0];
  assign DstReg = in_1[7:4];
  assign opCode = in_1[19:16];
  assign shiftAmount = in_1[3:0];
  assign SrcReg1 = in_1[15:12];
  assign SrcReg2 = in_1[11:8];
  assign TargetJump = in_1[15:8];
endmodule
